// Logisim project FSM.circ as structural Verilog: 5 circuits, main circuit FSM
module FSM (
  input  FSM_Input,
  output out_2
);

  wire clock_1_out;
  wire [1:0] fsmlogic_1_next_state, register_1_q;

  Register #(.width(2)) register_1 (.D(fsmlogic_1_next_state), .clk(clock_1_out), .Q(register_1_q));  // open: en, clr
  Clock clock_1 (.out(clock_1_out));
  FSMLogic fsmlogic_1 (
    .Input_Bit(FSM_Input), .Current_State(register_1_q), .Output(out_2), .Next_State(fsmlogic_1_next_state));
endmodule

// FSM Logic
module FSMLogic (
  input  Input_Bit,
  input  [1:0] Current_State,
  output Output,
  output [1:0] Next_State
);

  wire and_1_out, and_2_out, not_1_out, not_2_out, not_3_out;

  not not_1 (not_1_out, Current_State[1]);
  not not_2 (not_2_out, Input_Bit);
  not not_3 (not_3_out, Current_State[0]);
  and and_1 (and_1_out, Input_Bit, not_1_out);
  or or_1 (Output, and_1_out, and_2_out);
  and and_2 (and_2_out, not_2_out, not_3_out);
  StateBitZero statebitzero_1 (
    .Input(Input_Bit), .State_Bit_0(Current_State[0]), .State_Bit_1(Current_State[1]),
    .New_State_0(Next_State[0]));
  StateBitOne statebitone_1 (
    .Input(Input_Bit), .State_Bit_0(Current_State[0]), .State_Bit_1(Current_State[1]),
    .New_State_1(Next_State[1]));

  // Other names for the same wires on the sheet: Currrent_State_0 = Current_State[0];
  //   Current_State_1 = Current_State[1]
endmodule

// State Bit 1
module StateBitOne (
  input  Input,
  input  State_Bit_0,
  input  State_Bit_1,
  output New_State_1
);

  wire and_1_out, not_1_out;

  not not_1 (not_1_out, State_Bit_0);
  // NOT_Gate not_2 has open pins: in=State_Bit_1, out=open
  and and_1 (and_1_out, Input, not_1_out);
  or or_1 (New_State_1, and_1_out, State_Bit_0);

  // Notes on the sheet:
  //   PUT CIRCUITRY HERE
endmodule

// State Bit 0
module StateBitZero (
  input  Input,
  input  State_Bit_0,
  input  State_Bit_1,
  output New_State_0
);

  wire and_1_out, not_1_out, not_3_out;

  not not_1 (not_1_out, Input);
  // NOT_Gate not_2 has open pins: in=State_Bit_0, out=open
  not not_3 (not_3_out, State_Bit_1);
  and and_1 (and_1_out, not_1_out, not_3_out);
  or or_1 (New_State_0, and_1_out, State_Bit_1);

  // Notes on the sheet:
  //   PUT CIRCUITRY HERE
endmodule

module Ex4 (
  input  [7:0] In1,
  output Out1,
  output [7:0] Out2
);

  and and_1 (Out1, In1[0], In1[7]);
  not not_1 (Out2[7], In1[7]);

  assign Out2[6:0] = In1[6:0];
endmodule
