// Logisim project rotr.circ as structural Verilog: 5 circuits, main circuit main
module main (
  input  [15:0] A,
  input  [3:0] B,
  output [15:0] rotr_out
);

  wire [15:0] rotr1_1_out16, rotr2_1_out16, rotr4_1_out16;

  rotr1 rotr1_1 (.in16(A), .rotate(B[0]), .out16(rotr1_1_out16));
  rotr2 rotr2_1 (.in16(rotr1_1_out16), .rotate(B[1]), .out16(rotr2_1_out16));
  rotr4 rotr4_1 (.in16(rotr2_1_out16), .rotate(B[2]), .out16(rotr4_1_out16));
  rotr8 rotr8_1 (.in16(rotr4_1_out16), .rotate(B[3]), .out16(rotr_out));
endmodule

module rotr1 (
  input  [15:0] in16,
  input  rotate,
  output [15:0] out16
);

  Multiplexer #(.width(16), .enable("false")) multiplexer_1 (
    .in0(in16), .in1({in16[0], in16[15:1]}), .out(out16), .sel(rotate));
endmodule

module rotr2 (
  input  [15:0] in16,
  input  rotate,
  output [15:0] out16
);

  Multiplexer #(.width(16), .enable("false")) multiplexer_1 (
    .in0(in16), .in1({in16[1:0], in16[15:2]}), .out(out16), .sel(rotate));
endmodule

module rotr4 (
  input  [15:0] in16,
  input  rotate,
  output [15:0] out16
);

  Multiplexer #(.width(16), .enable("false")) multiplexer_1 (
    .in0(in16), .in1({in16[3:0], in16[15:4]}), .out(out16), .sel(rotate));
endmodule

module rotr8 (
  input  [15:0] in16,
  input  rotate,
  output [15:0] out16
);

  Multiplexer #(.width(16), .enable("false")) multiplexer_1 (
    .in0(in16), .in1({in16[7:0], in16[15:8]}), .out(out16), .sel(rotate));
endmodule
