// Logisim project work.circ as structural Verilog: 7 circuits, main circuit main
module main (
  input  in_1,
  input  in_2,
  input  in_3,
  input  in_4,
  input  in_5,
  input  in_6,
  input  in_7,
  input  in_8,
  input  in_9,
  input  in_10,
  input  in_11,
  output [7:0] out_12,
  output [7:0] out_13,
  output out_14,
  output out_15,
  output out_16
);

  NAND1 nand1_1 ();  // open: in_1, in_2, out_3
  NOR1 nor1_1 (.in_1(in_1), .in_2(in_2), .out_3(out_14));
  MUX2 mux2_1 (.s(in_3), .a(in_4), .b(in_5), .out_4(out_15));
  MUX4 mux4_1 (.s1(in_6), .s0(in_7), .a00(in_8), .a01(in_9), .a10(in_10), .a11(in_11), .out_7(out_16));
  AddMachine addmachine_1 (.out_1(out_12), .out_2(out_13));
endmodule

module NAND1 (
  input  in_1,
  input  in_2,
  output out_3
);

  wire and_1_out;

  and and_1 (and_1_out, in_1, in_2);
  not not_1 (out_3, and_1_out);
endmodule

module NOR1 (
  input  in_1,
  input  in_2,
  output out_3
);

  wire or_1_out;

  or or_1 (or_1_out, in_1, in_2);
  not not_1 (out_3, or_1_out);
endmodule

module XOR1 (
  input  in_1,
  input  in_2,
  output out_3
);

  wire and_1_out, and_2_out, not_1_out, not_2_out;

  not not_1 (not_1_out, in_1);
  not not_2 (not_2_out, in_2);
  and and_1 (and_1_out, not_1_out, in_2);
  and and_2 (and_2_out, in_1, not_2_out);
  or or_1 (out_3, and_1_out, and_2_out);
endmodule

module MUX2 (
  input  s,
  input  a,
  input  b,
  output out_4
);

  wire and_1_out, and_2_out, not_1_out;

  not not_1 (not_1_out, s);
  and and_1 (and_1_out, not_1_out, a);
  and and_2 (and_2_out, s, b);
  or or_1 (out_4, and_1_out, and_2_out);
endmodule

module MUX4 (
  input  s1,
  input  s0,
  input  a00,
  input  a01,
  input  a10,
  input  a11,
  output out_7
);

  wire mux2_1_out_4, mux2_2_out_4;

  MUX2 mux2_1 (.s(s0), .a(a00), .b(a01), .out_4(mux2_1_out_4));
  MUX2 mux2_2 (.s(s0), .a(a10), .b(a11), .out_4(mux2_2_out_4));
  MUX2 mux2_3 (.s(s1), .a(mux2_1_out_4), .b(mux2_2_out_4), .out_4(out_7));
endmodule

module AddMachine (
  output [7:0] out_1,
  output [7:0] out_2
);

  wire clock_1_out;

  Adder adder_1 (.a(8'h1), .b(out_2), .out(out_1));  // open: cin, cout
  Register register_1 (.D(out_1), .clk(clock_1_out), .Q(out_2));  // open: en, clr
  Clock clock_1 (.out(clock_1_out));
endmodule
