// Logisim project pipeline.circ as structural Verilog: 3 circuits, main circuit main
module main (
  output [7:0] Non_pipelined_Out,
  output [7:0] Pipelined_Out
);

  wire CLK_out;
  wire [7:0] Address_Counter_q, ROM_Unit_data;

  Clock CLK (.out(CLK_out));
  Counter Address_Counter (.clk(CLK_out), .Q(Address_Counter_q));  // open: clr, load, up, count, D, carry
  ROM ROM_Unit (.addr(Address_Counter_q), .data(ROM_Unit_data));
  Non_pipelined Non_pipelined (
    .In2(8'h1), .In3(ROM_Unit_data), .CLK(CLK_out), .Non_pipelined_Output(Non_pipelined_Out));
  Pipelined Pipelined1 (.In2(8'h1), .In3(ROM_Unit_data), .CLK(CLK_out), .Pipelined_Out(Pipelined_Out));

  // Notes on the sheet:
  //   contents of ROM_Unit (hex, n*v repeats v):
  //   3 2 fc 1 2 fb 1
endmodule

module Non_pipelined (
  input  [7:0] In2,
  input  [7:0] In3,
  input  CLK,
  output [7:0] Non_pipelined_Output
);

  wire [7:0] adder_1_out, multiplier_1_out;

  Multiplier multiplier_1 (.a(In2), .b(In3), .out(multiplier_1_out));  // open: cin, cout
  Register Non_pipelined_reg (.D(adder_1_out), .clk(CLK), .Q(Non_pipelined_Output));  // open: en, clr
  Adder adder_1 (.a(multiplier_1_out), .b(Non_pipelined_Output), .out(adder_1_out));  // open: cin, cout
endmodule

module Pipelined (
  input  [7:0] In2,
  input  [7:0] In3,
  input  CLK,
  output [7:0] Pipelined_Out
);

  wire [7:0] adder_1_out, multiplier_1_out, register_1_q;

  Register register_1 (.D(multiplier_1_out), .clk(CLK), .Q(register_1_q));  // open: en, clr
  Multiplier multiplier_1 (.a(In2), .b(In3), .out(multiplier_1_out));  // open: cin, cout
  Adder adder_1 (.a(register_1_q), .b(Pipelined_Out), .out(adder_1_out));  // open: cin, cout
  Register register_2 (.D(adder_1_out), .clk(CLK), .Q(Pipelined_Out));  // open: en, clr
endmodule
