// Logisim project alu.circ as structural Verilog: 1 circuit, main circuit alu
module alu (
  input  [31:0] A,
  input  [31:0] B,
  input  [3:0] ALUSel,
  output [31:0] Result,
  output [31:0] out_5,
  output [31:0] out_6,
  output [31:0] out_7,
  output [31:0] out_8,
  output [31:0] out_9,
  output [1:0] out_10,
  output [31:0] out_11
);

  wire comparator_1_lt;
  wire [31:0] add, and_0bdb476b, divu, mul, mulhu, multiplier_2_out, or_85264b1c, remu, sll_9f5e6f00, slt,
       sra_e0ffaae7, srl_d95d5ffd, sub, xor_d5b11f2b;

  Adder #(.width(32)) adder_1 (.a(A), .b(B), .out(add));  // open: cin, cout
  Subtractor #(.width(32)) subtractor_1 (.a(A), .b(B), .out(sub));  // open: bin, bout
  Multiplier #(.width(32)) multiplier_1 (.a(A), .b(B), .out(mul));  // open: cin, cout
  Divider #(.width(32)) divider_1 (.a(A), .b(B), .out(divu));  // open: upper, rem
  Comparator #(.width(32)) comparator_1 (.a(A), .b(B), .lt(comparator_1_lt));  // open: gt, eq
  Multiplier #(.width(32)) multiplier_2 (.a(B), .b(divu), .out(multiplier_2_out));  // open: cin, cout
  Multiplier #(.width(32)) multiplier_3 (.a(A), .b(B), .cout(mulhu));  // open: out, cin
  Multiplier #(.width(32)) multiplier_4 (.a(A), .b(B), .out(out_5), .cout(out_6));  // open: cin
  assign and_0bdb476b = A & B;  // AND_Gate and_1, 32 bits wide
  assign or_85264b1c = A | B;  // OR_Gate or_1, 32 bits wide
  assign xor_d5b11f2b = A ^ B;  // XOR_Gate xor_1, 32 bits wide
  Shifter #(.width(32), .shift("lr")) shifter_1 (.in(A), .\dist (B[4:0]), .out(srl_d95d5ffd));
  Shifter #(.width(32), .shift("ar")) shifter_2 (.in(A), .\dist (B[4:0]), .out(sra_e0ffaae7));
  Shifter #(.width(32)) shifter_3 (.in(A), .\dist (B[4:0]), .out(sll_9f5e6f00));
  assign slt = {{31{1'b0}}, comparator_1_lt};  // Bit_Extender bit_extender_1
  Subtractor #(.width(32)) subtractor_2 (.a(out_6), .b(A), .out(out_8));  // open: bin, bout
  Subtractor #(.width(32)) subtractor_3 (.a(out_6), .b(B), .out(out_9));  // open: bin, bout
  Subtractor #(.width(32)) subtractor_4 (.a(out_9), .b(A), .out(out_11));  // open: bin, bout
  Subtractor #(.width(32)) subtractor_5 (.a(A), .b(multiplier_2_out), .out(remu));  // open: bin, bout
  Multiplexer #(.select(2), .width(32), .enable("false")) multiplexer_1 (
    .in0(out_6), .in1(out_8), .in2(out_9), .in3(out_11), .out(out_7), .sel({A[31], B[31]}));
  Multiplexer #(.select(4), .width(32), .enable("false")) multiplexer_2 (
    .in0(add), .in1(and_0bdb476b), .in2(or_85264b1c), .in3(xor_d5b11f2b), .in4(srl_d95d5ffd),
    .in5(sra_e0ffaae7), .in6(sll_9f5e6f00), .in7(slt), .in8(divu), .in9(remu), .in10(mul), .in11(mulhu),
    .in12(sub), .in13(B), .in14(out_7), .out(Result), .sel(ALUSel));  // open: in15

  assign out_10 = {A[31], B[31]};

  // Other names for the same wires on the sheet: bsel[31:0] = B; mulh[31:0] = out_7

  // Notes on the sheet:
  //   INPUTS to your circuit
  //   DON'T CHANGE THE LOCATIONS OF THE INPUTS AND OUTPUTS!
  //   OUTPUT from your circuit
endmodule
