// Logisim project regfile.circ as structural Verilog: 1 circuit, main circuit main
module main (
  input  [4:0] rs1,
  input  [4:0] rs2,
  input  [4:0] rd,
  input  [31:0] Write_Data,
  input  RegWEn,
  input  clk,
  output [31:0] ra,
  output [31:0] sp,
  output [31:0] t0,
  output [31:0] t1,
  output [31:0] t2,
  output [31:0] s0,
  output [31:0] s1,
  output [31:0] a0,
  output [31:0] Read_Data_1,
  output [31:0] Read_Data_2
);

  wire enable1, enable2, enable5, enable6, enable7, enable8, enable9, enable10;
  wire [31:0] x0, x0_in, x1_in, x2_in, x5_in, x6_in, x7_in, x8_in, x9_in, x10_in;

  Multiplexer #(.select(5), .width(32), .enable("false")) multiplexer_1 (
    .in0(x0), .in1(ra), .in2(sp), .in5(t0), .in6(t1), .in7(t2), .in8(s0), .in9(s1), .in10(a0),
    .out(Read_Data_1), .sel(rs1));  // open: in3, in4, in11, in12, in13, in14, in15, in16, in17, in18, in19, in20, in21, in22, in23, in24, in25, in26, in27, in28, in29, in30, in31
  Register #(.width(32)) u_x0 (.D(x0_in), .en(1'b0), .clk(clk), .Q(x0));  // open: clr
  Register #(.width(32)) x1 (.D(x1_in), .en(enable1), .clk(clk), .Q(ra));  // open: clr
  Register #(.width(32)) x2 (.D(x2_in), .en(enable2), .clk(clk), .Q(sp));  // open: clr
  Register #(.width(32)) x5 (.D(x5_in), .en(enable5), .clk(clk), .Q(t0));  // open: clr
  Register #(.width(32)) x6 (.D(x6_in), .en(enable6), .clk(clk), .Q(t1));  // open: clr
  Register #(.width(32)) x7 (.D(x7_in), .en(enable7), .clk(clk), .Q(t2));  // open: clr
  Register #(.width(32)) x8 (.D(x8_in), .en(enable8), .clk(clk), .Q(s0));  // open: clr
  Register #(.width(32)) x9 (.D(x9_in), .en(enable9), .clk(clk), .Q(s1));  // open: clr
  Multiplexer #(.select(5), .width(32), .enable("false")) multiplexer_2 (
    .in0(x0), .in1(ra), .in2(sp), .in5(t0), .in6(t1), .in7(t2), .in8(s0), .in9(s1), .in10(a0),
    .out(Read_Data_2), .sel(rs2));  // open: in3, in4, in11, in12, in13, in14, in15, in16, in17, in18, in19, in20, in21, in22, in23, in24, in25, in26, in27, in28, in29, in30, in31
  Register #(.width(32)) x10 (.D(x10_in), .en(enable10), .clk(clk), .Q(a0));  // open: clr
  Demultiplexer #(.select(5), .width(32), .enable("false")) demultiplexer_1 (
    .out0(x0_in), .out1(x1_in), .out2(x2_in), .out5(x5_in), .out6(x6_in), .out7(x7_in), .out8(x8_in),
    .out9(x9_in), .out10(x10_in), .in(Write_Data), .sel(rd));  // open: out3, out4, out11, out12, out13, out14, out15, out16, out17, out18, out19, out20, out21, out22, out23, out24, out25, out26, out27, out28, out29, out30, out31
  Demultiplexer #(.select(5), .enable("false")) demultiplexer_2 (
    .out1(enable1), .out2(enable2), .out5(enable5), .out6(enable6), .out7(enable7), .out8(enable8),
    .out9(enable9), .out10(enable10), .in(RegWEn), .sel(rd));  // open: out0, out3, out4, out11, out12, out13, out14, out15, out16, out17, out18, out19, out20, out21, out22, out23, out24, out25, out26, out27, out28, out29, out30, out31

  // Other names for the same wires on the sheet: read_data1[31:0] = Read_Data_1; read_data2[31:0] = Read_Data_2;
  //   read_reg1[4:0] = rs1; read_reg2[4:0] = rs2; write_en = RegWEn; write_reg[4:0] = rd

  // Notes on the sheet:
  //   INPUTS to your circuit
  //   DON'T CHANGE THE LOCATIONS OF THE INPUTS AND OUTPUTS!
  //   These are DEBUG/TEST outputs from your circuit.
  //   OUTPUTS from your circuit
endmodule
