// Logisim project run.circ as structural Verilog: 1 circuit, main circuit main
module main (
  input  in_1,
  output [31:0] ra,
  output [31:0] sp,
  output [31:0] t0,
  output [31:0] t1,
  output [31:0] t2,
  output [31:0] s0,
  output [31:0] s1,
  output [31:0] a0,
  output [13:0] out_10,
  output [31:0] Requested_Address,
  output [31:0] Requested_Instruction,
  output [15:0] Time_Step,
  output halt
);

  Clock clock_1 ();  // open: out
  // Probe on {Requested_Address[31:14], out_10}
  ROM #(.addrWidth(14), .dataWidth(32)) rom_1 (.addr(out_10), .data(Requested_Instruction));
  cpu_main main_1 (
    .INSTRUCTION(Requested_Instruction), .CLOCK(in_1), .FETCH_ADDRESS({Requested_Address[31:14], out_10}),
    .ra(ra), .sp(sp), .t0(t0), .t1(t1), .t2(t2), .s0(s0), .s1(s1), .a0(a0));  // open: out_12, out_13
  // Probe on Requested_Instruction
  Counter #(.width(16), .max('hffff)) counter_1 (.clk(in_1), .Q(Time_Step));  // open: clr, load, up, count, D, carry
  Comparator #(.width(16)) comparator_1 (.a(Time_Step), .b(16'h100), .eq(halt));  // open: gt, lt

  assign Requested_Address[13:0] = out_10;

  // Other names for the same wires on the sheet: clk = in_1; fetch_addr[31:0] = {Requested_Address[31:14], out_10};
  //   Instruction[31:0] = Requested_Instruction

  // Notes on the sheet:
  //   contents of rom_1 (hex, n*v repeats v):
  //   840663 fff10113 fe000ee3 a48493 944a63 fe0008e3 fec48493 946a63 fe0002e3 1440413 fe84c8e3 fc000ce3
  //   533
  //   Instruction Memory
  //   YOUR CPU SHOULD FIT IN HERE!
  //   Halts Execution After Constant # of Clock Cycles
  //   Constant
endmodule
