// Logisim project cpu.circ as structural Verilog: 4 circuits, main circuit main
module main (
  input  [31:0] INSTRUCTION,
  input  CLOCK,
  output [31:0] FETCH_ADDRESS,
  output [31:0] ra,
  output [31:0] sp,
  output [31:0] t0,
  output [31:0] t1,
  output [31:0] t2,
  output [31:0] s0,
  output [31:0] s1,
  output [31:0] a0,
  output [31:0] out_12,
  output [31:0] out_13
);

  wire ASel, BrEQ, BrLT, BrUn, BSel, DMEM_p1, DMEM_p7, DMEM_p9, DMEM_p12, DMEM_p14, MemRW, PCSel, RegWEn;
  wire [1:0] WBSel;
  wire [2:0] ImmSel;
  wire [3:0] ALUSel;
  wire [31:0] adder_1_out, adder_2_out, ALU_Result, DMEM_p10, immgenerator_1_imm, multiplexer_1_out,
       multiplexer_2_out, multiplexer_3_out, multiplexer_4_out, PC_q, RegFile_read_data_1,
       RegFile_read_data_2, register_2_q, RegWriteD;

  Adder #(.width(32)) adder_1 (.a(PC_q), .b(32'h4), .out(adder_1_out));  // open: cin, cout
  Multiplexer #(.width(32), .enable("false")) multiplexer_1 (
    .in0(adder_1_out), .in1(ALU_Result), .out(multiplexer_1_out), .sel(PCSel));
  Multiplexer #(.width(32), .enable("false")) multiplexer_2 (
    .in0(INSTRUCTION), .in1(32'h13), .out(multiplexer_2_out), .sel(PCSel));
  Register #(.width(32)) PC (.D(multiplexer_1_out), .clk(CLOCK), .Q(PC_q));  // open: en, clr
  Register #(.width(32)) register_1 (.D(multiplexer_2_out), .clk(CLOCK), .Q(out_12));  // open: en, clr
  Shifter #(.width(32), .shift("ar")) shifter_1 (.in(PC_q), .\dist (5'b00010), .out(FETCH_ADDRESS));
  Register #(.width(32)) register_2 (.D(PC_q), .clk(CLOCK), .Q(register_2_q));  // open: en, clr
  regfile_main RegFile (
    .rs2(out_12[24:20]), .rd(out_12[11:7]), .Read_Data_1(RegFile_read_data_1),
    .Read_Data_2(RegFile_read_data_2), .ra(ra), .sp(sp), .t0(t0), .t1(t1), .t2(t2), .s0(s0), .s1(s1),
    .a0(a0), .rs1(out_12[19:15]), .Write_Data(RegWriteD), .RegWEn(RegWEn), .clk(CLOCK));
  ImmGenerator immgenerator_1 (.instruction(out_12), .ImmSel(ImmSel), .Imm(immgenerator_1_imm));
  Multiplexer #(.width(32), .enable("false")) multiplexer_3 (
    .in0(immgenerator_1_imm), .in1(RegFile_read_data_2), .out(multiplexer_3_out), .sel(BSel));
  MyComparator mycomparator_1 (
    .R1(RegFile_read_data_1), .R2(RegFile_read_data_2), .BrUn(BrUn), .BrLT(BrLT), .BrEQ(BrEQ));
  Multiplexer #(.width(32), .enable("false")) multiplexer_4 (
    .in0(register_2_q), .in1(RegFile_read_data_1), .out(multiplexer_4_out), .sel(ASel));
  Adder #(.width(32)) adder_2 (.a(32'h4), .b(register_2_q), .out(adder_2_out));  // open: cin, cout
  alu alu_1 (
    .A(multiplexer_4_out), .B(multiplexer_3_out), .ALUSel(ALUSel), .Result(ALU_Result));  // open: out_5, out_6, out_7, out_8, out_9, out_10, out_11
  control control_1 (
    .instruction(out_12), .BrEQ(BrEQ), .BrLT(BrLT), .PCSel(PCSel), .ImmSel(ImmSel), .BrUn(BrUn), .ASel(ASel),
    .BSel(BSel), .MemRW(MemRW), .RegWEn(RegWEn), .ALUSel(ALUSel), .WBSel(WBSel));
  // mem_main DMEM: pin names not known; wires that end beside it: DMEM_p1, ALU_Result, RegFile_read_data_2, MemRW, CLOCK, DMEM_p1, DMEM_p7, DMEM_p7, DMEM_p9, DMEM_p10, DMEM_p9, DMEM_p12, DMEM_p12, DMEM_p14
  Multiplexer #(.select(2), .width(32), .enable("false")) multiplexer_5 (
    .in0(DMEM_p10), .in1(ALU_Result), .in2(adder_2_out), .out(RegWriteD), .sel(WBSel));  // open: in3

  // Other names for the same wires on the sheet: clk = CLOCK; fetch_addr[31:0] = FETCH_ADDRESS;
  //   rd[4:0] = out_12[11:7]; rs1[4:0] = out_12[19:15]; rs2[4:0] = out_12[24:20]

  // Notes on the sheet:
  //   Output
  //   Inputs/Outputs from run.circ. DO NOT MOVE THESE.
  //   Inputs
  //   It is OK to move the PC, RegFile, ALU, and MEM to wherever is most convenient for you when constructing your CPU, and to delete this text
  //   Inputs/Outputs from run.circ. DO NOT MOVE THESE.
endmodule

module control (
  input  [31:0] instruction,
  input  BrEQ,
  input  BrLT,
  output PCSel,
  output [2:0] ImmSel,
  output BrUn,
  output ASel,
  output BSel,
  output MemRW,
  output RegWEn,
  output [3:0] ALUSel,
  output [1:0] WBSel
);

  wire and_1_out, and_3_out, and_4_out, and_5_out, and_6_out, and_7_out, and_8_out, and_9_out, and_10_out,
       and_11_out, and_12_out, and_13_out, and_14_out, and_15_out, and_16_out, comparator_1_eq,
       comparator_2_eq, comparator_3_eq, comparator_4_eq, comparator_5_eq, comparator_6_eq, comparator_7_eq,
       comparator_8_eq, comparator_9_eq, comparator_10_eq, comparator_11_eq, comparator_12_eq,
       comparator_15_eq, comparator_16_eq, comparator_17_eq, comparator_18_eq, comparator_19_eq,
       comparator_20_eq, comparator_21_eq, comparator_22_eq, comparator_23_eq, comparator_25_eq,
       comparator_26_eq, comparator_27_eq, comparator_28_eq, comparator_29_eq, comparator_30_eq,
       comparator_31_eq, comparator_32_eq, comparator_33_eq, comparator_34_eq, comparator_35_eq,
       comparator_36_eq, comparator_37_eq, comparator_38_eq, comparator_39_eq, comparator_40_eq,
       comparator_41_eq, comparator_42_eq, comparator_43_eq, comparator_44_eq, comparator_45_eq,
       comparator_46_eq, comparator_47_eq, comparator_48_eq, comparator_49_eq, comparator_50_eq,
       comparator_51_eq, comparator_52_eq, comparator_53_eq, comparator_54_eq, comparator_55_eq,
       comparator_56_eq, comparator_57_eq, comparator_58_eq, comparator_59_eq, comparator_60_eq,
       comparator_61_eq, comparator_62_eq, comparator_63_eq, comparator_64_eq, comparator_65_eq,
       comparator_66_eq, not_1_out, not_2_out, not_3_out, not_4_out, or_1_out, or_2_out, or_9_out, or_10_out,
       or_12_out, or_13_out, or_14_out, or_15_out;

  Comparator #(.width(5), .mode("unsigned")) comparator_1 (
    .a(instruction[6:2]), .b(5'b01100), .eq(comparator_1_eq));  // open: gt, lt
  Comparator #(.width(5), .mode("unsigned")) comparator_2 (
    .a(instruction[6:2]), .b(5'b01101), .eq(comparator_2_eq));  // open: gt, lt
  Comparator #(.width(5), .mode("unsigned")) comparator_3 (
    .a(instruction[6:2]), .b(5'b01100), .eq(comparator_3_eq));  // open: gt, lt
  Comparator #(.width(3), .mode("unsigned")) comparator_4 (
    .a(instruction[14:12]), .b(3'b000), .eq(comparator_4_eq));  // open: gt, lt
  Comparator #(.width(5), .mode("unsigned")) comparator_5 (
    .a(instruction[6:2]), .b(5'b01100), .eq(comparator_5_eq));  // open: gt, lt
  Comparator #(.width(5), .mode("unsigned")) comparator_6 (
    .a(instruction[6:2]), .b(5'b00100), .eq(comparator_6_eq));  // open: gt, lt
  Comparator #(.width(5), .mode("unsigned")) comparator_7 (
    .a(instruction[6:2]), .b(5'b11000), .eq(comparator_7_eq));  // open: gt, lt
  Comparator #(.width(5), .mode("unsigned")) comparator_8 (
    .a(instruction[6:2]), .b(5'b01100), .eq(comparator_8_eq));  // open: gt, lt
  Comparator #(.width(5), .mode("unsigned")) comparator_9 (
    .a(instruction[6:2]), .b(5'b00100), .eq(comparator_9_eq));  // open: gt, lt
  Comparator #(.width(5), .mode("unsigned")) comparator_10 (
    .a(instruction[6:2]), .b({5{1'b0}}), .eq(comparator_10_eq));  // open: gt, lt
  Comparator #(.width(5), .mode("unsigned")) comparator_11 (
    .a(instruction[6:2]), .b(5'b01000), .eq(comparator_11_eq));  // open: gt, lt
  Comparator #(.width(5), .mode("unsigned")) comparator_12 (
    .a(instruction[6:2]), .b(5'b11001), .eq(comparator_12_eq));  // open: gt, lt
  Comparator #(.width(5), .mode("unsigned")) comparator_13 (
    .a(instruction[6:2]), .b(5'b01100), .eq(BSel));  // open: gt, lt
  Comparator #(.width(5), .mode("unsigned")) comparator_14 (
    .a(instruction[6:2]), .b(5'b01000), .eq(MemRW));  // open: gt, lt
  Comparator #(.width(5), .mode("unsigned")) comparator_15 (
    .a(instruction[6:2]), .b(5'b01100), .eq(comparator_15_eq));  // open: gt, lt
  Comparator #(.width(5), .mode("unsigned")) comparator_16 (
    .a(instruction[6:2]), .b(5'b00100), .eq(comparator_16_eq));  // open: gt, lt
  Comparator #(.width(5), .mode("unsigned")) comparator_17 (
    .a(instruction[6:2]), .b({5{1'b0}}), .eq(comparator_17_eq));  // open: gt, lt
  Comparator #(.width(5), .mode("unsigned")) comparator_18 (
    .a(instruction[6:2]), .b(5'b11001), .eq(comparator_18_eq));  // open: gt, lt
  Comparator #(.width(5), .mode("unsigned")) comparator_19 (
    .a(instruction[6:2]), .b(5'b11011), .eq(comparator_19_eq));  // open: gt, lt
  Comparator #(.width(5), .mode("unsigned")) comparator_20 (
    .a(instruction[6:2]), .b(5'b01101), .eq(comparator_20_eq));  // open: gt, lt
  Comparator #(.width(5), .mode("unsigned")) comparator_21 (
    .a(instruction[6:2]), .b(5'b11000), .eq(comparator_21_eq));  // open: gt, lt
  Comparator #(.width(5), .mode("unsigned")) comparator_22 (
    .a(instruction[6:2]), .b(5'b11001), .eq(comparator_22_eq));  // open: gt, lt
  Comparator #(.width(5), .mode("unsigned")) comparator_23 (
    .a(instruction[6:2]), .b(5'b11011), .eq(comparator_23_eq));  // open: gt, lt
  Comparator #(.width(5), .mode("unsigned")) comparator_24 (
    .a(instruction[6:2]), .b(5'b11011), .eq(ImmSel[2]));  // open: gt, lt
  Comparator #(.width(5), .mode("unsigned")) comparator_25 (
    .a(instruction[6:2]), .b(5'b11000), .eq(comparator_25_eq));  // open: gt, lt
  Comparator #(.width(5), .mode("unsigned")) comparator_26 (
    .a(instruction[6:2]), .b(5'b01101), .eq(comparator_26_eq));  // open: gt, lt
  Comparator #(.width(5), .mode("unsigned")) comparator_27 (
    .a(instruction[6:2]), .b(5'b01000), .eq(comparator_27_eq));  // open: gt, lt
  Comparator #(.width(5), .mode("unsigned")) comparator_28 (
    .a(instruction[6:2]), .b(5'b01101), .eq(comparator_28_eq));  // open: gt, lt
  Comparator #(.width(5), .mode("unsigned")) comparator_29 (
    .a(instruction[6:2]), .b(5'b11001), .eq(comparator_29_eq));  // open: gt, lt
  Comparator #(.width(5), .mode("unsigned")) comparator_30 (
    .a(instruction[6:2]), .b(5'b11011), .eq(comparator_30_eq));  // open: gt, lt
  Comparator #(.width(5), .mode("unsigned")) comparator_31 (
    .a(instruction[6:2]), .b(5'b01100), .eq(comparator_31_eq));  // open: gt, lt
  Comparator #(.width(5), .mode("unsigned")) comparator_32 (
    .a(instruction[6:2]), .b(5'b00100), .eq(comparator_32_eq));  // open: gt, lt
  Comparator #(.width(5), .mode("unsigned")) comparator_33 (
    .a(instruction[6:2]), .b(5'b01101), .eq(comparator_33_eq));  // open: gt, lt
  and and_1 (and_1_out, comparator_1_eq, instruction[25]);
  or or_1 (or_1_out, comparator_5_eq, comparator_6_eq);
  Comparator #(.width(5), .mode("unsigned")) comparator_34 (
    .a(instruction[6:2]), .b(5'b01100), .eq(comparator_34_eq));  // open: gt, lt
  Comparator #(.width(3), .mode("unsigned")) comparator_35 (
    .a(instruction[14:12]), .b(3'b000), .eq(comparator_35_eq));  // open: gt, lt
  Comparator #(.width(5), .mode("unsigned")) comparator_36 (
    .a(instruction[6:2]), .b(5'b01101), .eq(comparator_36_eq));  // open: gt, lt
  Comparator #(.width(5), .mode("unsigned")) comparator_37 (
    .a(instruction[6:2]), .b(5'b01100), .eq(comparator_37_eq));  // open: gt, lt
  Comparator #(.width(3), .mode("unsigned")) comparator_38 (
    .a(instruction[14:12]), .b(3'b001), .eq(comparator_38_eq));  // open: gt, lt
  Comparator #(.width(5), .mode("unsigned")) comparator_39 (
    .a(instruction[6:2]), .b(5'b01100), .eq(comparator_39_eq));  // open: gt, lt
  Comparator #(.width(5), .mode("unsigned")) comparator_40 (
    .a(instruction[6:2]), .b(5'b00100), .eq(comparator_40_eq));  // open: gt, lt
  Comparator #(.width(5), .mode("unsigned")) comparator_41 (
    .a(instruction[6:2]), .b(5'b01100), .eq(comparator_41_eq));  // open: gt, lt
  or or_2 (or_2_out, comparator_41_eq, comparator_42_eq);
  Comparator #(.width(5), .mode("unsigned")) comparator_42 (
    .a(instruction[6:2]), .b(5'b00100), .eq(comparator_42_eq));  // open: gt, lt
  Comparator #(.width(5), .mode("unsigned")) comparator_43 (
    .a(instruction[6:2]), .b(5'b01100), .eq(comparator_43_eq));  // open: gt, lt
  and and_2 (BrUn, comparator_7_eq, instruction[13], instruction[14]);
  or or_3 (ASel, comparator_8_eq, comparator_9_eq, comparator_10_eq, comparator_11_eq, comparator_12_eq);
  or or_4 (RegWEn, comparator_15_eq, comparator_16_eq, comparator_17_eq, comparator_18_eq, comparator_19_eq, comparator_20_eq);
  or or_5 (ImmSel[1], comparator_25_eq, comparator_26_eq);
  or or_6 (ImmSel[0], comparator_27_eq, comparator_28_eq);
  or or_7 (WBSel[1], comparator_29_eq, comparator_30_eq);
  or or_8 (WBSel[0], comparator_31_eq, comparator_32_eq, comparator_33_eq);
  and and_3 (and_3_out, comparator_3_eq, instruction[30], comparator_4_eq);
  Comparator #(.width(3), .mode("unsigned")) comparator_44 (
    .a(instruction[14:12]), .b(3'b101), .eq(comparator_44_eq));  // open: gt, lt
  Comparator #(.width(3), .mode("unsigned")) comparator_45 (
    .a(instruction[14:12]), .b(3'b001), .eq(comparator_45_eq));  // open: gt, lt
  Comparator #(.width(3), .mode("unsigned")) comparator_46 (
    .a(instruction[14:12]), .b(3'b010), .eq(comparator_46_eq));  // open: gt, lt
  and and_4 (and_4_out, comparator_34_eq, instruction[30], comparator_35_eq);
  or or_9 (or_9_out, comparator_39_eq, comparator_40_eq);
  Comparator #(.width(5), .mode("unsigned")) comparator_47 (
    .a(instruction[6:2]), .b(5'b01100), .eq(comparator_47_eq));  // open: gt, lt
  Comparator #(.width(3), .mode("unsigned")) comparator_48 (
    .a(instruction[14:12]), .b(3'b000), .eq(comparator_48_eq));  // open: gt, lt
  not not_1 (not_1_out, BrEQ);
  Comparator #(.width(3), .mode("unsigned")) comparator_49 (
    .a(instruction[14:12]), .b(3'b101), .eq(comparator_49_eq));  // open: gt, lt
  not not_2 (not_2_out, instruction[30]);
  or or_10 (or_10_out, comparator_44_eq, comparator_45_eq, comparator_46_eq);
  and and_5 (and_5_out, comparator_37_eq, instruction[25], comparator_38_eq);
  Comparator #(.width(3), .mode("unsigned")) comparator_50 (
    .a(instruction[14:12]), .b(3'b000), .eq(comparator_50_eq));  // open: gt, lt
  Comparator #(.width(3), .mode("unsigned")) comparator_51 (
    .a(instruction[14:12]), .b(3'b011), .eq(comparator_51_eq));  // open: gt, lt
  Comparator #(.width(3), .mode("unsigned")) comparator_52 (
    .a(instruction[14:12]), .b(3'b001), .eq(comparator_52_eq));  // open: gt, lt
  Comparator #(.width(3), .mode("unsigned")) comparator_53 (
    .a(instruction[14:12]), .b(3'b111), .eq(comparator_53_eq));  // open: gt, lt
  Comparator #(.width(3), .mode("unsigned")) comparator_54 (
    .a(instruction[14:12]), .b(3'b011), .eq(comparator_54_eq));  // open: gt, lt
  Comparator #(.width(3), .mode("unsigned")) comparator_55 (
    .a(instruction[14:12]), .b(3'b001), .eq(comparator_55_eq));  // open: gt, lt
  Comparator #(.width(3), .mode("unsigned")) comparator_56 (
    .a(instruction[14:12]), .b(3'b100), .eq(comparator_56_eq));  // open: gt, lt
  Comparator #(.width(3), .mode("unsigned")) comparator_57 (
    .a(instruction[14:12]), .b(3'b110), .eq(comparator_57_eq));  // open: gt, lt
  or or_11 (ALUSel[3], and_1_out, comparator_2_eq, and_3_out);
  and and_6 (and_6_out, or_1_out, not_2_out, or_10_out);
  not not_3 (not_3_out, instruction[30]);
  Comparator #(.width(3), .mode("unsigned")) comparator_58 (
    .a(instruction[14:12]), .b(3'b110), .eq(comparator_58_eq));  // open: gt, lt
  Comparator #(.width(3), .mode("unsigned")) comparator_59 (
    .a(instruction[14:12]), .b(3'b100), .eq(comparator_59_eq));  // open: gt, lt
  Comparator #(.width(3), .mode("unsigned")) comparator_60 (
    .a(instruction[14:12]), .b(3'b001), .eq(comparator_60_eq));  // open: gt, lt
  Comparator #(.width(3), .mode("unsigned")) comparator_61 (
    .a(instruction[14:12]), .b(3'b010), .eq(comparator_61_eq));  // open: gt, lt
  or or_12 (or_12_out, comparator_50_eq, comparator_51_eq, comparator_52_eq);
  not not_4 (not_4_out, instruction[30]);
  Comparator #(.width(3), .mode("unsigned")) comparator_62 (
    .a(instruction[14:12]), .b(3'b111), .eq(comparator_62_eq));  // open: gt, lt
  Comparator #(.width(3), .mode("unsigned")) comparator_63 (
    .a(instruction[14:12]), .b(3'b100), .eq(comparator_63_eq));  // open: gt, lt
  Comparator #(.width(3), .mode("unsigned")) comparator_64 (
    .a(instruction[14:12]), .b(3'b010), .eq(comparator_64_eq));  // open: gt, lt
  Comparator #(.width(3), .mode("unsigned")) comparator_65 (
    .a(instruction[14:12]), .b(3'b101), .eq(comparator_65_eq));  // open: gt, lt
  or or_13 (or_13_out, comparator_53_eq, comparator_54_eq);
  Comparator #(.width(5), .mode("unsigned")) comparator_66 (
    .a(instruction[6:2]), .b(5'b01101), .eq(comparator_66_eq));  // open: gt, lt
  and and_7 (and_7_out, comparator_21_eq, comparator_48_eq, BrEQ);
  and and_8 (and_8_out, comparator_21_eq, comparator_55_eq, not_1_out);
  and and_9 (and_9_out, comparator_21_eq, comparator_56_eq, BrLT);
  and and_10 (and_10_out, comparator_21_eq, comparator_57_eq, BrLT);
  and and_11 (and_11_out, or_1_out, instruction[30], comparator_49_eq);
  or or_14 (or_14_out, comparator_58_eq, comparator_59_eq, comparator_60_eq, comparator_61_eq);
  and and_12 (and_12_out, comparator_47_eq, instruction[25], or_12_out);
  and and_13 (and_13_out, or_2_out, not_4_out, or_15_out);
  or or_15 (or_15_out, comparator_62_eq, comparator_63_eq, comparator_64_eq);
  and and_14 (and_14_out, comparator_43_eq, instruction[25], or_13_out);
  or or_16 (ALUSel[2], and_11_out, and_6_out, and_4_out, comparator_36_eq, and_5_out);
  and and_15 (and_15_out, or_9_out, not_3_out, or_14_out);
  and and_16 (and_16_out, or_2_out, instruction[30], comparator_65_eq);
  or or_17 (PCSel, and_7_out, and_8_out, and_9_out, and_10_out, comparator_22_eq, comparator_23_eq);
  or or_18 (ALUSel[0], and_13_out, and_16_out, and_14_out, comparator_66_eq);
  or or_19 (ALUSel[1], and_15_out, and_12_out);

  // Other names for the same wires on the sheet: opcode[4:0] = instruction[6:2]; funct3[2:0] = instruction[14:12];
  //   flag25 = instruction[25]; flag30 = instruction[30]

  // Notes on the sheet:
  //   01100
  //   00100
  //   00000
  //   01000
  //   11000
  //   11011
  //   11001
  //   01101
  //   Input
  //   Output Control Signals
endmodule

module ImmGenerator (
  input  [31:0] instruction,
  input  [2:0] ImmSel,
  output [31:0] Imm
);

  wire [31:0] bit_extender_1_out, bit_extender_2_out, bit_extender_3_out, bit_extender_4_out,
       bit_extender_5_out, shifter_1_out;

  assign bit_extender_1_out = {{12{1'b0}}, instruction[31:12]};  // Bit_Extender bit_extender_1
  assign bit_extender_2_out = {{20{instruction[31]}}, instruction[31:20]};  // Bit_Extender bit_extender_2
  assign bit_extender_3_out = {{20{instruction[31]}}, {instruction[31:25], instruction[11:7]}};  // Bit_Extender bit_extender_3
  assign bit_extender_4_out = {{19{instruction[31]}}, {instruction[31], instruction[7], instruction[30:25], instruction[11:8], 1'b0}};  // Bit_Extender bit_extender_4
  Shifter #(.width(32)) shifter_1 (.in(bit_extender_1_out), .\dist (5'b01100), .out(shifter_1_out));
  assign bit_extender_5_out = {{11{instruction[31]}}, {instruction[31], instruction[19:12], instruction[20], instruction[30:21], 1'b0}};  // Bit_Extender bit_extender_5
  Multiplexer #(.select(3), .width(32), .enable("false")) multiplexer_1 (
    .in0(bit_extender_2_out), .in1(bit_extender_3_out), .in2(bit_extender_4_out), .in3(shifter_1_out),
    .in4(bit_extender_5_out), .out(Imm), .sel(ImmSel));  // open: in5, in6, in7
endmodule

module MyComparator (
  input  [31:0] R1,
  input  [31:0] R2,
  input  BrUn,
  output BrLT,
  output BrEQ
);

  wire comparator_1_eq, comparator_1_lt, comparator_2_eq, comparator_2_lt;

  Comparator #(.width(32)) comparator_1 (.a(R1), .b(R2), .eq(comparator_1_eq), .lt(comparator_1_lt));  // open: gt
  Comparator #(.width(32), .mode("unsigned")) comparator_2 (
    .a(R1), .b(R2), .eq(comparator_2_eq), .lt(comparator_2_lt));  // open: gt
  Multiplexer #(.enable("false")) multiplexer_1 (.in0(comparator_1_lt), .in1(comparator_2_lt), .out(BrLT), .sel(BrUn));
  Multiplexer #(.enable("false")) multiplexer_2 (.in0(comparator_1_eq), .in1(comparator_2_eq), .out(BrEQ), .sel(BrUn));
endmodule
